# Fritzing sketch SODAR_diagrama (saved by Fritzing 0.9.0b)
breadboards: 1

parts:
  Parte1 = Arduino Uno (Rev3)
  Parte2 = SRF05 Ultrasonic Rangefinder
  J2 = Basic Servo

nets:
  N1: Parte1.D8, Parte2.Trig
  N2: Parte1.D9_PWM, J2.pulse
  N3: Parte1.D7, Parte2.Echo
  VCC: Parte1.5V, Parte2.VCC, J2.vcc
  GND: Parte1.GND, Parte2.GND, J2.gnd
